// Logisim project Proj 1.circ as structural Verilog: 12 circuits, main circuit main
module main (
  input  [31:0] FromMem,
  output WED
);

  wire clock_1_out, decode_1_mux1, decode_1_mux2, decode_1_shiftamt, decode_1_signed, decode_1_writeenable1,
       decode_1_writeenable2, isolate34_1_wbmux_out, isolate34_1_wer_out, isolator_2_3_1_ie_out,
       isolator_2_3_1_wbmux_out, isolator_2_3_1_wed_out, isolator_2_3_1_wer_out, registerfile_1_p3;
  wire [3:0] decode_1_alu_code, isolator_2_3_1_op_out;
  wire [4:0] isolate34_1_rd_out, isolator_2_3_1_rd_out, isolator_2_3_1_rs_out, isolator_2_3_1_rt_out,
       isolator_2_3_1_sa_out, registerfile_1_p4, savar_1_sa_out, split_1_rd, split_1_rs, split_1_rt,
       split_1_shamt;
  wire [5:0] split_1_func, split_1_op;
  wire [15:0] isolator_2_3_1_imm_out, split_1_imm;
  wire [31:0] bit_extender_1_out, count_1_1_pc_4, forward_1_forwarded, forward_2_forwarded,
       isolate12_1_instr_out, isolate12_1_pc_out, isolate34_1_c_out, isolate34_1_pc_out,
       isolator_2_3_1_a_out, isolator_2_3_1_b_out, isolator_2_3_1_pc_out, mips_alu_1_p5, mipsprogramrom_1_p2,
       multiplexer_1_out, multiplexer_2_out, register_1_q, registerfile_1_p1, registerfile_1_p7,
       registerfile_1_p8;

  Clock clock_1 (.out(clock_1_out));
  Count__1 count_1_1 (.PC(register_1_q), .PC_4(count_1_1_pc_4));
  Register #(.width(32)) register_1 (.D(count_1_1_pc_4), .Q(register_1_q), .clk(clock_1_out));  // open: en, clr
  // MIPSProgramROM mipsprogramrom_1: pin names not known; wires that end beside it: register_1_q, mipsprogramrom_1_p2
  Isolate12 isolate12_1 (
    .PC_in(register_1_q), .Instr_in(mipsprogramrom_1_p2), .clock(clock_1_out), .PC_out(isolate12_1_pc_out),
    .Instr_out(isolate12_1_instr_out));
  Split split_1 (
    .Instr(isolate12_1_instr_out), .rs(split_1_rs), .rt(split_1_rt), .shamt(split_1_shamt), .rd(split_1_rd),
    .Imm(split_1_imm), .Op(split_1_op), .Func(split_1_func));
  Decode decode_1 (
    .Op(split_1_op), .Func(split_1_func), .ShiftAmt(decode_1_shiftamt), .ALU_code(decode_1_alu_code),
    .MUX1(decode_1_mux1), .MUX2(decode_1_mux2), .WriteEnable1(decode_1_writeenable1),
    .WriteEnable2(decode_1_writeenable2), .Signed(decode_1_signed));
  // RegisterFile registerfile_1: pin names not known; wires that end beside it: registerfile_1_p1, clock_1_out, registerfile_1_p3, registerfile_1_p4, split_1_rs, split_1_rt, registerfile_1_p7, registerfile_1_p8
  SAVar savar_1 (.Select(decode_1_shiftamt), .SA_in(split_1_shamt), .A_in(registerfile_1_p7), .SA_out(savar_1_sa_out));
  Isolator_2_3 isolator_2_3_1 (
    .rs_in(split_1_rs), .rt_in(split_1_rt), .PC_in(isolate12_1_pc_out), .Imm_in(split_1_imm),
    .A_in(registerfile_1_p7), .B_in(registerfile_1_p8), .rd_in(split_1_rd), .sa_in(savar_1_sa_out),
    .op_in(decode_1_alu_code), .IE_in(decode_1_mux1), .WBMUX_in(decode_1_mux2),
    .WER_in(decode_1_writeenable1), .WED_in(decode_1_writeenable2), .Signed_in(decode_1_signed),
    .clock(clock_1_out), .rs_out(isolator_2_3_1_rs_out), .rt_out(isolator_2_3_1_rt_out),
    .PC_out(isolator_2_3_1_pc_out), .Imm_out(isolator_2_3_1_imm_out), .A_out(isolator_2_3_1_a_out),
    .B_out(isolator_2_3_1_b_out), .rd_out(isolator_2_3_1_rd_out), .sa_out(isolator_2_3_1_sa_out),
    .op_out(isolator_2_3_1_op_out), .IE_out(isolator_2_3_1_ie_out), .WBMUX_out(isolator_2_3_1_wbmux_out),
    .WER_out(isolator_2_3_1_wer_out), .WED_out(isolator_2_3_1_wed_out));  // open: Signed_out
  Forward forward_1 (
    .Out2(registerfile_1_p1), .rd2(registerfile_1_p4), .rd1(isolate34_1_rd_out), .Out1(isolate34_1_c_out),
    .rs(isolator_2_3_1_rs_out), .Out0(isolator_2_3_1_a_out), .Forwarded(forward_1_forwarded));
  Forward forward_2 (
    .Out2(registerfile_1_p1), .rd2(registerfile_1_p4), .rd1(isolate34_1_rd_out), .Out1(isolate34_1_c_out),
    .rs(isolator_2_3_1_rt_out), .Out0(isolator_2_3_1_b_out), .Forwarded(forward_2_forwarded));
  assign bit_extender_1_out = {{16{1'b0}}, isolator_2_3_1_imm_out};  // Bit_Extender bit_extender_1
  Multiplexer #(.width(32), .enable("false")) multiplexer_1 (
    .in0(forward_2_forwarded), .in1(bit_extender_1_out), .out(multiplexer_1_out), .sel(isolator_2_3_1_ie_out));
  // Mips_ALU mips_alu_1: pin names not known; wires that end beside it: forward_1_forwarded, multiplexer_1_out, isolator_2_3_1_op_out, isolator_2_3_1_sa_out, mips_alu_1_p5
  Isolate_45 isolate_45_1 (
    .C_in(multiplexer_2_out), .PC_in(isolate34_1_pc_out), .rd_in(isolate34_1_rd_out),
    .WER_in(isolate34_1_wer_out), .clock(clock_1_out), .C_out(registerfile_1_p1), .rd_out(registerfile_1_p4),
    .WER_out(registerfile_1_p3));  // open: PC_out
  Isolate34 isolate34_1 (
    .C_in(mips_alu_1_p5), .PC_in(isolator_2_3_1_pc_out), .rd_in(isolator_2_3_1_rd_out),
    .WBMUX_in(isolator_2_3_1_wbmux_out), .WER_in(isolator_2_3_1_wer_out), .WED_in(isolator_2_3_1_wed_out),
    .clock(clock_1_out), .C_out(isolate34_1_c_out), .PC_out(isolate34_1_pc_out), .rd_out(isolate34_1_rd_out),
    .WBMUX_out(isolate34_1_wbmux_out), .WER_out(isolate34_1_wer_out), .WED_out(WED));
  Multiplexer #(.width(32), .enable("false")) multiplexer_2 (
    .in0(isolate34_1_c_out), .in1(FromMem), .out(multiplexer_2_out), .sel(isolate34_1_wbmux_out));
endmodule

module Count__1 (
  input  [31:0] PC,
  output [31:0] PC_4
);

  // Incrementer incrementer_1: pin names not known; wires that end beside it: PC[31:2], PC_4[31:2]

  assign PC_4[1:0] = PC[1:0];
endmodule

module Split (
  input  [31:0] Instr,
  output [4:0] rs,
  output [4:0] rt,
  output [4:0] shamt,
  output [4:0] rd,
  output [15:0] Imm,
  output [5:0] Op,
  output [5:0] Func
);


  assign Func = Instr[5:0];
  assign Imm = Instr[15:0];
  assign Op = Instr[31:26];
  assign rd = Instr[15:11];
  assign rs = Instr[25:21];
  assign rt = Instr[20:16];
  assign shamt = Instr[10:6];
endmodule

module Isolator_2_3 (
  input  [4:0] rs_in,
  input  [4:0] rt_in,
  input  [31:0] PC_in,
  input  [15:0] Imm_in,
  input  [31:0] A_in,
  input  [31:0] B_in,
  input  [4:0] rd_in,
  input  [4:0] sa_in,
  input  [3:0] op_in,
  input  IE_in,
  input  WBMUX_in,
  input  WER_in,
  input  WED_in,
  input  Signed_in,
  input  clock,
  output [4:0] rs_out,
  output [4:0] rt_out,
  output [31:0] PC_out,
  output [15:0] Imm_out,
  output [31:0] A_out,
  output [31:0] B_out,
  output [4:0] rd_out,
  output [4:0] sa_out,
  output [3:0] op_out,
  output IE_out,
  output WBMUX_out,
  output WER_out,
  output WED_out,
  output Signed_out
);

  Register #(.width(5)) rs (.D(rs_in), .Q(rs_out), .clk(clock));  // open: en, clr
  Register #(.width(5)) rt (.D(rt_in), .Q(rt_out), .clk(clock));  // open: en, clr
  Register #(.width(32)) PC (.D(PC_in), .Q(PC_out), .clk(clock));  // open: en, clr
  Register #(.width(16)) Imm (.D(Imm_in), .Q(Imm_out), .clk(clock));  // open: en, clr
  Register #(.width(32)) A (.D(A_in), .Q(A_out), .clk(clock));  // open: en, clr
  Register #(.width(32)) B (.D(B_in), .Q(B_out), .clk(clock));  // open: en, clr
  Register #(.width(5)) rd (.D(rd_in), .Q(rd_out), .clk(clock));  // open: en, clr
  Register #(.width(5)) sa (.D(sa_in), .Q(sa_out), .clk(clock));  // open: en, clr
  Register #(.width(4)) aluop (.D(op_in), .Q(op_out), .clk(clock));  // open: en, clr
  Register #(.width(1)) IE (.D(IE_in), .Q(IE_out), .clk(clock));  // open: en, clr
  Register #(.width(1)) WBMUX (.D(WBMUX_in), .Q(WBMUX_out), .clk(clock));  // open: en, clr
  Register #(.width(1)) WER (.D(WER_in), .Q(WER_out), .clk(clock));  // open: en, clr
  Register #(.width(1)) WED (.D(WED_in), .Q(WED_out), .clk(clock));  // open: en, clr
  Register #(.width(1)) Signed (.D(Signed_in), .Q(Signed_out), .clk(clock));  // open: en, clr
endmodule

module Isolate34 (
  input  [31:0] C_in,
  input  [31:0] PC_in,
  input  [4:0] rd_in,
  input  WBMUX_in,
  input  WER_in,
  input  WED_in,
  input  clock,
  output [31:0] C_out,
  output [31:0] PC_out,
  output [4:0] rd_out,
  output WBMUX_out,
  output WER_out,
  output WED_out
);

  Register #(.width(32)) PC (.D(C_in), .Q(C_out), .clk(clock));  // open: en, clr
  Register #(.width(32)) PC_2 (.D(PC_in), .Q(PC_out), .clk(clock));  // open: en, clr
  Register #(.width(5)) rd (.D(rd_in), .Q(rd_out), .clk(clock));  // open: en, clr
  Register #(.width(1)) WBMUX (.D(WBMUX_in), .Q(WBMUX_out), .clk(clock));  // open: en, clr
  Register #(.width(1)) WER (.D(WER_in), .Q(WER_out), .clk(clock));  // open: en, clr
  Register #(.width(1)) WED (.D(WED_in), .Q(WED_out), .clk(clock));  // open: en, clr
endmodule

module Isolate_45 (
  input  [31:0] C_in,
  input  [31:0] PC_in,
  input  [4:0] rd_in,
  input  WER_in,
  input  clock,
  output [31:0] C_out,
  output [31:0] PC_out,
  output [4:0] rd_out,
  output WER_out
);

  Register #(.width(32)) PC (.D(C_in), .Q(C_out), .clk(clock));  // open: en, clr
  Register #(.width(32)) PC_2 (.D(PC_in), .Q(PC_out), .clk(clock));  // open: en, clr
  Register #(.width(5)) rd (.D(rd_in), .Q(rd_out), .clk(clock));  // open: en, clr
  Register #(.width(1)) WER (.D(WER_in), .Q(WER_out), .clk(clock));  // open: en, clr
endmodule

module Forward (
  input  [31:0] Out2,
  input  [4:0] rd2,
  input  [4:0] rd1,
  input  [31:0] Out1,
  input  [4:0] rs,
  input  [31:0] Out0,
  output [31:0] Forwarded
);

  wire nor_1_out, nor_2_out;
  wire [4:0] xor_1_out, xor_2_out;
  wire [31:0] multiplexer_1_out;

  assign xor_1_out = rd1 ^ rs;  // XOR_Gate xor_1, 5 bits wide
  assign xor_2_out = rs ^ rd2;  // XOR_Gate xor_2, 5 bits wide
  nor nor_1 (nor_1_out, xor_1_out[0], xor_1_out[1], xor_1_out[2], xor_1_out[3], xor_1_out[4]);
  nor nor_2 (nor_2_out, xor_2_out[0], xor_2_out[1], xor_2_out[2], xor_2_out[3], xor_2_out[4]);
  Multiplexer #(.width(32), .enable("false")) multiplexer_1 (
    .in0(Out0), .in1(Out2), .out(multiplexer_1_out), .sel(nor_2_out));
  Multiplexer #(.width(32), .enable("false")) multiplexer_2 (
    .in0(multiplexer_1_out), .in1(Out1), .out(Forwarded), .sel(nor_1_out));
endmodule

module Isolate12 (
  input  [31:0] PC_in,
  input  [31:0] Instr_in,
  input  clock,
  output [31:0] PC_out,
  output [31:0] Instr_out
);

  Register #(.width(32)) PC (.D(PC_in), .Q(PC_out), .clk(clock));  // open: en, clr
  Register #(.width(32)) Instr (.D(Instr_in), .Q(Instr_out), .clk(clock));  // open: en, clr
endmodule

module Decode (
  input  [5:0] Op,
  input  [5:0] Func,
  output ShiftAmt,
  output [3:0] ALU_code,
  output MUX1,
  output MUX2,
  output WriteEnable1,
  output WriteEnable2,
  output Signed
);

  wire i_j_out_1_mux1, i_j_out_1_mux2, i_j_out_1_sa, i_j_out_1_signed, i_j_out_1_we1, i_j_out_1_we2,
       nor_1_out, r_out_1_mux1, r_out_1_mux2, r_out_1_sa, r_out_1_signed, r_out_1_we1, r_out_1_we2;
  wire [3:0] i_j_out_1_o0, r_out_1_o0;

  nor nor_1 (nor_1_out, Op[0], Op[1], Op[2], Op[3], Op[4], Op[5]);
  I___J_Out i_j_out_1 (
    .B0(Op[0]), .B1(Op[1]), .B2(Op[2]), .B3(Op[3]), .B4(Op[4]), .B5(Op[5]), .O0(i_j_out_1_o0[0]),
    .O1(i_j_out_1_o0[1]), .O2(i_j_out_1_o0[2]), .O3(i_j_out_1_o0[3]), .MUX1(i_j_out_1_mux1),
    .MUX2(i_j_out_1_mux2), .SA(i_j_out_1_sa), .Signed(i_j_out_1_signed), .WE1(i_j_out_1_we1),
    .WE2(i_j_out_1_we2));
  R_Out r_out_1 (
    .B0(Func[0]), .B1(Func[1]), .B2(Func[2]), .B3(Func[3]), .B4(Func[4]), .B5(Func[5]), .O0(r_out_1_o0[0]),
    .O1(r_out_1_o0[1]), .O2(r_out_1_o0[2]), .O3(r_out_1_o0[3]), .MUX1(r_out_1_mux1), .MUX2(r_out_1_mux2),
    .SA(r_out_1_sa), .Signed(r_out_1_signed), .WE1(r_out_1_we1), .WE2(r_out_1_we2));
  Multiplexer #(.width(4), .enable("false")) multiplexer_1 (
    .in0(i_j_out_1_o0), .in1(r_out_1_o0), .out(ALU_code), .sel(nor_1_out));
  Multiplexer #(.enable("false")) multiplexer_2 (.in0(i_j_out_1_mux1), .in1(r_out_1_mux1), .out(MUX1), .sel(nor_1_out));
  Multiplexer #(.enable("false")) multiplexer_3 (.in0(i_j_out_1_mux2), .in1(r_out_1_mux2), .out(MUX2), .sel(nor_1_out));
  Multiplexer #(.enable("false")) multiplexer_4 (.in0(i_j_out_1_sa), .in1(r_out_1_sa), .out(ShiftAmt), .sel(nor_1_out));
  Multiplexer #(.enable("false")) multiplexer_5 (
    .in0(i_j_out_1_signed), .in1(r_out_1_signed), .out(Signed), .sel(nor_1_out));
  Multiplexer #(.enable("false")) multiplexer_6 (
    .in0(i_j_out_1_we1), .in1(r_out_1_we1), .out(WriteEnable1), .sel(nor_1_out));
  Multiplexer #(.enable("false")) multiplexer_7 (
    .in0(i_j_out_1_we2), .in1(r_out_1_we2), .out(WriteEnable2), .sel(nor_1_out));
endmodule

module I___J_Out (
  input  B0,
  input  B1,
  input  B2,
  input  B3,
  input  B4,
  input  B5,
  output O0,
  output O1,
  output O2,
  output O3,
  output MUX1,
  output MUX2,
  output SA,
  output Signed,
  output WE1,
  output WE2
);

  wire and_2_out, and_3_out, and_4_out, and_5_out, and_6_out, and_7_out, and_8_out, nor_1_out, not_1_out,
       not_2_out, not_3_out, not_4_out, not_5_out, not_6_out, not_7_out, not_8_out, not_9_out, not_10_out,
       not_11_out, not_12_out, not_13_out, not_14_out, not_15_out, not_16_out, not_17_out, not_18_out,
       not_19_out, not_20_out, not_21_out, not_22_out, not_23_out, or_1_out, or_2_out;

  not not_1 (not_1_out, B5);
  not not_2 (not_2_out, B4);
  not not_3 (not_3_out, B2);
  not not_4 (not_4_out, B1);
  not not_5 (not_5_out, B2);
  not not_6 (not_6_out, B0);
  not not_7 (not_7_out, B2);
  not not_8 (not_8_out, B2);
  not not_9 (not_9_out, B1);
  not not_10 (not_10_out, B5);
  not not_11 (not_11_out, B4);
  not not_12 (not_12_out, B5);
  not not_13 (not_13_out, B4);
  not not_14 (not_14_out, B5);
  not not_15 (not_15_out, B4);
  not not_16 (not_16_out, B2);
  not not_17 (not_17_out, B0);
  and and_1 (O0, not_1_out, not_2_out, B3, not_3_out, B1);
  and and_2 (and_2_out, not_4_out, B0);
  and and_3 (and_3_out, not_5_out, B1);
  and and_4 (and_4_out, B2, B1, B0);
  and and_5 (and_5_out, B2, B1, not_6_out);
  and and_6 (and_6_out, not_7_out, B1);
  and and_7 (and_7_out, not_8_out, not_9_out, B0);
  and and_8 (and_8_out, B2, B1, B0);
  and and_9 (MUX1, not_10_out, not_11_out, B3);
  and and_10 (MUX2, not_12_out, not_13_out, B3, B2, B1, B0);
  and and_11 (Signed, not_14_out, not_15_out, B3, not_16_out, B1, not_17_out);
  not not_18 (not_18_out, B5);
  not not_19 (not_19_out, B4);
  or or_1 (or_1_out, and_2_out, and_3_out, and_4_out);
  not not_20 (not_20_out, B5);
  not not_21 (not_21_out, B4);
  or or_2 (or_2_out, and_5_out, and_6_out);
  not not_22 (not_22_out, B5);
  not not_23 (not_23_out, B4);
  nor nor_1 (nor_1_out, and_7_out, and_8_out);
  and and_12 (O1, not_18_out, not_19_out, B3, or_1_out);
  and and_13 (O2, not_20_out, not_21_out, B3, or_2_out);
  and and_14 (O3, not_22_out, not_23_out, B3, nor_1_out);

  assign SA = 1'b1;
  assign WE1 = 1'b1;
  assign WE2 = 1'b0;
endmodule

module R_Out (
  input  B0,
  input  B1,
  input  B2,
  input  B3,
  input  B4,
  input  B5,
  output O0,
  output O1,
  output O2,
  output O3,
  output MUX1,
  output MUX2,
  output SA,
  output Signed,
  output WE1,
  output WE2
);

  wire and_1_out, and_2_out, and_3_out, and_4_out, and_5_out, and_6_out, and_7_out, and_8_out, and_9_out,
       and_10_out, and_11_out, and_12_out, and_15_out, and_16_out, and_17_out, and_18_out, and_19_out,
       nand_1_out, not_1_out, not_2_out, not_3_out, not_4_out, not_5_out, not_6_out, not_7_out, not_8_out,
       not_9_out, not_10_out, not_11_out, not_12_out, not_13_out, not_14_out, not_15_out, not_16_out,
       not_17_out, not_18_out, not_19_out, not_20_out, not_21_out, not_22_out, not_23_out, not_24_out,
       not_25_out, not_26_out, not_27_out, not_28_out, not_29_out, not_30_out, not_31_out, not_32_out,
       not_33_out, not_34_out, not_35_out, not_36_out, not_37_out, not_38_out, or_2_out, or_3_out;

  not not_1 (not_1_out, B4);
  not not_2 (not_2_out, B2);
  not not_3 (not_3_out, B5);
  not not_4 (not_4_out, B4);
  not not_5 (not_5_out, B2);
  not not_6 (not_6_out, B5);
  not not_7 (not_7_out, B4);
  not not_8 (not_8_out, B3);
  not not_9 (not_9_out, B2);
  not not_10 (not_10_out, B1);
  not not_11 (not_11_out, B2);
  not not_12 (not_12_out, B1);
  not not_13 (not_13_out, B2);
  not not_14 (not_14_out, B4);
  not not_15 (not_15_out, B3);
  not not_16 (not_16_out, B4);
  not not_17 (not_17_out, B2);
  not not_18 (not_18_out, B1);
  not not_19 (not_19_out, B4);
  not not_20 (not_20_out, B2);
  not not_21 (not_21_out, B0);
  and and_1 (and_1_out, B5, not_1_out, B3, not_2_out, B1);
  and and_2 (and_2_out, not_3_out, not_4_out, B3, not_5_out, B1);
  and and_3 (and_3_out, not_6_out, not_7_out, not_8_out, B1, B0);
  and and_4 (and_4_out, not_9_out, not_10_out, B0);
  and and_5 (and_5_out, not_11_out, B1, B0);
  and and_6 (and_6_out, B2, not_12_out, B0);
  and and_7 (and_7_out, B2, B1, B0);
  not not_22 (not_22_out, B5);
  and and_8 (and_8_out, not_22_out, not_23_out);
  not not_23 (not_23_out, B0);
  and and_9 (and_9_out, not_13_out, B1, B0);
  and and_10 (and_10_out, B2, B1);
  and and_11 (and_11_out, B5, not_14_out, not_15_out, B2);
  and and_12 (and_12_out, not_16_out, B3, not_17_out, B1);
  not not_24 (not_24_out, B5);
  not not_25 (not_25_out, B4);
  not not_26 (not_26_out, B3);
  nand nand_1 (nand_1_out, not_18_out, B0);
  and and_13 (Signed, B5, not_19_out, B3, not_20_out, B1, not_21_out);
  or or_1 (O0, and_1_out, and_2_out, and_3_out);
  not not_27 (not_27_out, B4);
  not not_28 (not_28_out, B3);
  or or_2 (or_2_out, and_4_out, and_5_out, and_6_out, and_7_out);
  not not_29 (not_29_out, and_8_out);
  not not_30 (not_30_out, B4);
  not not_31 (not_31_out, B2);
  not not_32 (not_32_out, B4);
  not not_33 (not_33_out, B3);
  or or_3 (or_3_out, and_9_out, and_10_out);
  not not_34 (not_34_out, B4);
  not not_35 (not_35_out, B2);
  not not_36 (not_36_out, B5);
  not not_37 (not_37_out, B4);
  not not_38 (not_38_out, B3);
  or or_4 (O3, and_11_out, and_12_out);
  and and_14 (SA, not_24_out, not_25_out, not_26_out, B2, nand_1_out);
  and and_15 (and_15_out, B5, not_27_out, not_28_out, or_2_out);
  and and_16 (and_16_out, not_29_out, not_30_out, B3, not_31_out, B1);
  and and_17 (and_17_out, B5, not_32_out, not_33_out, or_3_out);
  and and_18 (and_18_out, B5, not_34_out, B3, not_35_out, B1);
  and and_19 (and_19_out, not_36_out, not_37_out, not_38_out, B1);
  or or_5 (O1, and_15_out, and_16_out);
  or or_6 (O2, and_17_out, and_18_out, and_19_out);

  assign MUX1 = 1'b0;
  assign MUX2 = 1'b0;
  assign WE1 = 1'b1;
  assign WE2 = 1'b0;
endmodule

module SAVar (
  input  [4:0] SA_in,
  input  [31:0] A_in,
  input  Select,
  output [4:0] SA_out
);

  Multiplexer #(.width(5)) multiplexer_1 (.in0(SA_in), .in1(A_in[4:0]), .out(SA_out), .sel(Select));  // open: en
endmodule
